# Fritzing sketch Desk_Thermometer_Diagram (saved by Fritzing 0.9.6b)
breadboards: 1

parts:
  Part1 = Arduino Uno (Rev3) - ICSP
  DHT11_1 = DHT11 module
  PIR1 = PIR sensor
  U1 = LCD-16X2 [package=lcd-16x2_noholes]
  R1 = Rotary Potentiometer (Small) [maximum_resistance=100kΩ package=THT]
  R2 = Resistor [tolerance=±5% resistance=1k package="1206 [SMD]"]

nets:
  N1: Part1.ICSP_MOSI, Part1.D11_PWM/MOSI, U1.DB5
  N2: Part1.D10_PWM/SS, U1.DB4
  N3: Part1.D12/MISO, U1.DB6
  N4: Part1.D13/SCK, U1.DB7
  N5: Part1.D2, DHT11_1.VCC
  N6: Part1.D4, U1.RS
  N7: Part1.D6_PWM, U1.E
  N8: Part1.D7, PIR1.SIG
  N9: Part1.3V3, U1.A
  VDD: Part1.5V, DHT11_1.DATA, PIR1.VDD, U1.VDD, R1.leg1
  GND: Part1.GND, DHT11_1.GND, PIR1.GND, U1.VSS, U1.R_W, R1.leg2, R2.Pin_0
  N10: U1.VO, R2.Pin_1
  N11: U1.K, R1.wiper

custom parts:
  DHT11 module: https://cdn-learn.adafruit.com/downloads/pdf/dht.pdf DHT11 black pcb module reference by:https://github.com/adafruit/Fritzing-Library/blob/master/parts/DHT11%20Humitidy%20and%20Temperature%20Sensor.fzpz
